# Fritzing sketch pir_sensor (saved by Fritzing 0.8.5b)
breadboards: 1

parts:
  WeMos_D1_Mini3 = WeMos D1 Mini
  R1 = Photocell (LDR) [package=THT]
  R2 = Resistor [package="0402 [SMD]"]
  Connector_for_PIR_Sensor = Header 3 [package=molex-1x3_lock]

nets:
  N1: WeMos_D1_Mini3.3V3, R1.pin_0, Connector_for_PIR_Sensor.1
  N2: WeMos_D1_Mini3.A0, R1.pin_1, R2.Pin_0
  N3: WeMos_D1_Mini3.D5, Connector_for_PIR_Sensor.2
  N4: WeMos_D1_Mini3.G, R2.Pin_1, Connector_for_PIR_Sensor.3

custom parts:
  WeMos D1 Mini: The D1 mini is a mini wifi board based on ESP-8266EX.
